# Fritzing sketch fritz_dual_flywheel (saved by Fritzing 0.9.10b)
breadboards: 1

parts:
  Part1 = Adafruit Metro with Headers [part_number="Adafruit #2488"]
  M1 = roboclaw_2x45a
  M2 = roboclaw_2x45a
  Mod1 = flyskyr6b
  M3 = gear-motor
  M4 = gear-motor
  M5 = gear-motor
  M6 = gear-motor
  BATT1 = 4xAA Switchable Battery Pack w/Bare Wire

nets:
  N1: Part1.SCK, Mod1.CH6
  N2: Part1.MISO, Mod1.CH5
  N3: Part1.MOSI, Mod1.CH2
  N4: Part1.SS, Mod1.CH1
  N5: Part1.IO3, M1.S2-Sig
  N6: Part1.IO2, M1.S1-Sig
  N7: Part1.IO1, M2.S2-Sig
  N8: Part1.IO0, M2.S1-Sig
  N9: Part1.+5V, Mod1.BAT+
  GND: Part1.GND, M1.S1-GND, M1.S5-GND, M1.BAT_-, M2.EN2_-, M2.S1-GND, M2.S5-GND, M2.BAT_-, Mod1.GND, BATT1.POS
  N10: M1.M1_A, M5.pin_2
  N11: M1.M1_B, M5.pin_1
  N12: M1.BAT_+, M2.BAT_+, BATT1.NEG
  N13: M1.M2_A, M6.pin_1
  N14: M1.M2_B, M6.pin_2
  N15: M2.M1_A, M4.pin_2
  N16: M2.M1_B, M4.pin_1
  N17: M2.M2_A, M3.pin_2
  N18: M2.M2_B, M3.pin_1

notes:
  Drive train Motors
  LEFT
  RIGHT
  FlyWheel 1
  FlyWheel 2 (if necessary)
  FlySky

custom parts:
  Adafruit Metro with Headers: We sure love the ATmega328 here at Adafruit, and we use them a lot for our own projects. The processor has plenty of GPIO, Analog inputs, hardware UART SPI and I2C, timers and PWM galore - just enough for most simple projects. When we need to go small, we use a Pro Trinket 3V or 5V, but when size isn't as much of a concern, and an USB-serial converter is required, we reach for an Adafruit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
  roboclaw_2x45a: Roboclaw 2x45 motor driver.
  flyskyr6b: flysky r6b 6ch rc receiver module. Pcb view is 3*7 header pins, 3 female headers will let the board plug in to the receiver, or connect via wires as you choose.
  4xAA Switchable Battery Pack w/Bare Wire: 4xAA Switchable Battery Pack with Bare Wire connection
